# Fritzing sketch ItsyBitsy_v1 (saved by Fritzing 0.9.3b)
breadboards: 1

parts:
  Part1 = Black Joystick KY-023
  Part2 = Itsy Bitsy M0 Express
  Part3 = Display LED de 8 dígitos basado en MAX7219  # not connected

nets:
  N1: Part1.SW, Part2.A0
  N2: Part1.VRy, Part2.A1
  N3: Part1.VRx, Part2.A2
  +5V: Part1.+5V, Part2.+3V3
  GND: Part1.GND, Part2.GND

custom parts:
  Black Joystick KY-023: Description: The joystick is a combination of 2 analoog potentiometer and a digital switch. Arduino GND --> Module pin - Arduino +5V --> Module pin +5V Arduino Analoog 0 --> Module VRx Arduino Analoog 1 --> Module VRy Arduino Digital --> Module SW Dimensions: 1" x 1.25"
  Itsy Bitsy M0 Express: What's smaller than a Feather but larger than a Trinket? It's an Adafruit ItsyBitsy M0 Express! Small, powerful, with a rockin' ATSAMD21 Cortex M0 processor running at 48 MHz - this microcontroller board is perfect when you want something very compact, but still with a bunch of pins. ItsyBitsy M0 Express is only 1.4" long by 0.7" wide, but has 6 power pins, 23 digital GPIO pins (12 of which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
