# Fritzing sketch TinkerKit_v1 (saved by Fritzing 0.9.3b)
breadboards: 1

parts:
  Part1 = Adafruit Trinket M0 [part_number="Adafruit #3500"]
  Part2 = Mini 8x8 LED Matrix Backpack [part_number=871]
  Part4 = Black Joystick KY-023

nets:
  GND: Part1.GND, Part2.GND, Part4.GND
  N1: Part1.D4_A2_PA06_TXD_MOSI, Part4.VRx
  N2: Part1.D3_A3_PA07_RXD_SCK, Part4.VRy
  3.3V: Part1.3.3V, Part2.VDD, Part4.+5V
  N3: Part1.D2_A1_PA09_SCL_MISO, Part2.SCL
  N4: Part1.D1_A0_PA02, Part4.SW
  N5: Part1.D0_A4_PA08_SDA, Part2.SDA

custom parts:
  Mini 8x8 LED Matrix Backpack: This 0.8" 8x8 monochrome LED matrix includes a driver chip for simple control via an I2C interface. The backpack features address-selection jumpers so you can connect up to four matrices on a single I2C bus.
  Black Joystick KY-023: Description: The joystick is a combination of 2 analoog potentiometer and a digital switch. Arduino GND --> Module pin - Arduino +5V --> Module pin +5V Arduino Analoog 0 --> Module VRx Arduino Analoog 1 --> Module VRy Arduino Digital --> Module SW Dimensions: 1" x 1.25"
